# Fritzing sketch mod2 (saved by Fritzing 0.9.3b)
breadboards: 1

parts:
  U1 = NodeMCU V3.0
  R1 = Photocell (LDR) [package=THT]
  R2 = Resistor [tolerance=±5% resistance=10k package="0805 [SMD]"]
  IR1 = TSOP312.., 314.. [package=THT]
  LED1 = LEDs [package=led10mm]
  R3 = Resistor [tolerance=±5% resistance=470 package="0805 [SMD]"]

nets:
  N1: U1.D2, R3.Pin_0
  N2: U1.3V3, R1.pin_1, IR1.Data
  N3: U1.GND#6, U1.GND#13, U1.GND#16, U1.GND#33, R2.Pin_0, IR1.Vs, LED1.C
  N4: U1.D5, IR1.GND
  N5: U1.A0, R1.pin_0, R2.Pin_1
  N6: LED1.A, R3.Pin_1

notes:
  Resistor 10k Ω
  Resistor 470 Ω

custom parts:
  NodeMCU V3.0: ESP8266 based NodeMCU
